# Fritzing sketch fish (saved by Fritzing 0.9.5d)
breadboards: 1

parts:
  Mod1 = Raspberry Pi 4B  # not connected
  Componente1 = Arduino Mega 2560 (Rev3)
  HC-SR04_Sensor_1 = HC-SR04 Ultrasonic Distance Sensor
  HC-SR04_Sensor_2 = HC-SR04 Ultrasonic Distance Sensor
  HC-SR04_Sensor_3 = HC-SR04 Ultrasonic Distance Sensor
  HC-SR04_Sensor_4 = HC-SR04 Ultrasonic Distance Sensor
  HC-SR04_Sensor_5 = HC-SR04 Ultrasonic Distance Sensor
  HC-SR04_Sensor_6 = HC-SR04 Ultrasonic Distance Sensor
  HC-SR04_Sensor_7 = HC-SR04 Ultrasonic Distance Sensor
  HC-SR04_Sensor_8 = HC-SR04 Ultrasonic Distance Sensor
  USBTTL1 = USB A Plug
  USBTTL2 = Micro USB B Plug
  M2 = DC Motor  # not connected
  M5 = DC Motor  # not connected
  IC1 = Rasberry Pi NIOR Camera [chip_label=IC package="DIP (Dual Inline) [THT]"]  # not connected
  M6 = DC Motor  # not connected
  M7 = DC Motor  # not connected
  A1 = L298N DC motor driver  # not connected
  A2 = L298N DC motor driver  # not connected

nets:
  VCC: Componente1.5V, HC-SR04_Sensor_1.VCC, HC-SR04_Sensor_2.VCC, HC-SR04_Sensor_3.VCC, HC-SR04_Sensor_4.VCC, HC-SR04_Sensor_5.VCC, HC-SR04_Sensor_6.VCC, HC-SR04_Sensor_7.VCC, HC-SR04_Sensor_8.VCC
  GND: Componente1.GND, HC-SR04_Sensor_1.GND, HC-SR04_Sensor_2.GND, HC-SR04_Sensor_3.GND, HC-SR04_Sensor_4.GND, HC-SR04_Sensor_5.GND, HC-SR04_Sensor_6.GND, HC-SR04_Sensor_7.GND, HC-SR04_Sensor_8.GND
  N1: Componente1.D24, HC-SR04_Sensor_3.TRIG
  N2: Componente1.D25, HC-SR04_Sensor_3.ECHO
  N3: Componente1.D28, HC-SR04_Sensor_8.TRIG
  N4: Componente1.D29, HC-SR04_Sensor_8.ECHO
  N5: Componente1.D32, HC-SR04_Sensor_5.TRIG
  N6: Componente1.D33, HC-SR04_Sensor_5.ECHO
  N7: Componente1.D36, HC-SR04_Sensor_6.TRIG
  N8: Componente1.D37, HC-SR04_Sensor_6.ECHO
  N9: Componente1.D40, HC-SR04_Sensor_7.TRIG
  N10: Componente1.D41, HC-SR04_Sensor_7.ECHO
  N11: Componente1.D44, HC-SR04_Sensor_2.TRIG
  N12: Componente1.D45, HC-SR04_Sensor_2.ECHO
  N13: Componente1.D48, HC-SR04_Sensor_4.TRIG
  N14: Componente1.D49, HC-SR04_Sensor_4.ECHO
  N15: Componente1.D52, HC-SR04_Sensor_1.TRIG
  N16: Componente1.D53, HC-SR04_Sensor_1.ECHO
  N17: USBTTL1.usb, USBTTL2.usb

custom parts:
  Rasberry Pi NIOR Camera: Camera
  L298N DC motor driver: This L298N Motor Driver Module is a high power motor driver module for driving DC and Stepper Motors. This module consists of an L298 motor driver IC and a 78M05 5V regulator.
